# Fritzing sketch WaterHeater (saved by Fritzing 0.9.3b)

parts:
  Mod1 = Arduino Sensor Shield v5.0
  A1 = BBAA100043
  Mod2 = KY-004 Key Switch Module [package="Breakout board"]  # not connected
  Mod3 = KY-004 Key Switch Module [package="Breakout board"]  # not connected
  Mod4 = KY-004 Key Switch Module [package="Breakout board"]  # not connected
  Mod5 = KY-019 5V Relay Module [package="Breakout board"]  # not connected
  Mod6 = KY-015 Temperature & Humidity Sensor Module [package="Breakout board"]  # not connected

nets:
  N1: Mod1.A5-GND, Mod1.0-G, A1.pin4
  N2: Mod1.10-S, A1.pin2
  N3: Mod1.9-S, A1.pin1

custom parts:
  Arduino Sensor Shield v5.0: Arduino Sensor Shield v5.0 provides I2C interface, Bluetooth module communication interface, SD card module communication interface, APC220 wireless RF modules communication interface, RB URF V1.1 ultrasonic sensors interface, 12864 LCD serial and parallel interface, 32 servo controller interfaces. In addition (with the sel jumper removed) allows an external power supply for the servos as the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
  BBAA100043: BBAA100043 traffic light module.
  KY-004 Key Switch Module: Arduino Key Switch Module Keyes KY-004 is a push button that will output a high signal when pressed.
  KY-019 5V Relay Module: KY-019 5V Relay module, used to control AC circuits. (Special thanks to vanepp for fixing the PCB holes and other errors)
  KY-015 Temperature & Humidity Sensor Module: KY-015 temperature and humidity sensor module, provides a low-latency serial interface to measure humidity and temperature.
